# Fritzing sketch bar-o-matic (saved by Fritzing 0.9.2b)

parts:
  Composant1 = Arduino Mega 2560 (Rev3)
  MD09B1 = A4988 Stepper Motor Driver Carrier
  M1 = Stepper Motor - Bipolar
  Composant2 = HX711 Weighing Sensor Module
  Load_Cell1 = Load Cell - Red/white/black/green
  Composant3 = NeoPixel Stick [part_number=1426]
  J13 = Basic Servo
  J14 = Basic Servo
  J16 = Basic Servo
  J17 = Basic Servo
  J18 = Basic Servo
  J19 = Basic Servo
  J20 = Basic Servo
  J21 = Basic Servo
  J22 = Basic Servo
  Composant4 = NeoPixel Stick [part_number=1426]
  J23 = Power Jack [package=power_jack_pth_lock]
  J15 = Basic Servo
  C1 = Capacitor Polarized [package=panasonic_c]  # not connected
  D2F1 = D2F-FL Omron Snap Action Limit Switch with Level
  R1 = Resistor [tolerance=±5% resistance=10k package="1206 [SMD]"]
  Raspberry_Pi1 = Raspberry Pi 2  # not connected

nets:
  N1: Composant1.D21/SCL, Composant2.CK/TX
  N2: Composant1.D20/SDA, Composant2.DO/RX
  N3: Composant1.D13_PWM, J13.pulse
  N4: Composant1.D12_PWM, J14.pulse
  N5: Composant1.D11_PWM, J15.pulse
  N6: Composant1.D10_PWM, J16.pulse
  N7: Composant1.D9_PWM, J17.pulse
  N8: Composant1.D8_PWM, J22.pulse
  5V: Composant1.5V, Composant2.VCC
  N9: Composant1.GND, MD09B1.GROUND#147
  N10: Composant1.D2_PWM, MD09B1.STEP
  N11: Composant1.D3_PWM, MD09B1.DIR
  N12: Composant1.D4_PWM, J18.pulse
  N13: Composant1.D5_PWM, J19.pulse
  N14: Composant1.D6_PWM, J20.pulse
  N15: Composant1.D7_PWM, J21.pulse
  N16: Composant1.D44, Composant4.DATAIN
  N17: Composant1.D45, Composant3.DATAIN
  N18: Composant1.D53, D2F1.COM
  N19: MD09B1.RESET, MD09B1.SLEEP
  N20: MD09B1.OUT_2B, M1.A
  N21: MD09B1.OUT_2A, M1.C
  N22: MD09B1.OUT_1A, M1.B
  N23: MD09B1.OUT_1B, M1.D
  N24: Composant2.A+, Load_Cell1.wire1
  N25: Composant2.A-, Load_Cell1.wire2
  N26: Composant2.B+, Load_Cell1.wire3
  N27: Composant2.B-, Load_Cell1.wire4
  GND: J16.gnd, J17.gnd, J23.GND
  VCC: J17.vcc, J23.PWR, J15.vcc
  N28: D2F1.NC, R1.Pin_0

custom parts:
  Load Cell - Red/white/black/green: A rectangle load cell/weighting pressure Sensor with four wires - Red, white, black, green. Normally corresponding with E+, E-, A+, A- respectively.
  NeoPixel Stick: Make your own little LED strip arrangement with this stick of NeoPixel LEDs. We crammed 8 of the tiny 5050 (5mm x 5mm) smart RGB LEDs onto a PCB with mounting holes and a chainable design. Use only one microcontroller pin to control as many as you can chain together! Each LED is addressable as the driver chip is inside the LED. Each one has ~18mA constant current drive so the color will be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
  D2F-FL Omron Snap Action Limit Switch with Level: Snap action switch with stainless steel lever.
